# Fritzing sketch motionsense (saved by Fritzing 0.9.3b)

parts:
  Raspberry_Pi_1 = Raspberry Pi 3 [part_number=RPI-3-V1.2]
  PIR2 = PIR sensor

nets:
  N1: Raspberry_Pi_1.GPIO4, PIR2.SIG
  GND: Raspberry_Pi_1.GND, PIR2.GND
  5V: Raspberry_Pi_1.5V, PIR2.VDD

notes:
  Attach camera to camera port.
